# Fritzing sketch semaphore (saved by Fritzing 0.9.0b)
circuit board: 8.46667cm x 5.64444cm
breadboards: 1

parts:
  XTAL1 = Crystal [frequency="16 MHz" package=THT]
  R1 = Resistor [tolerance=±5% resistance=68 package=THT]
  R2 = Resistor [tolerance=±5% resistance=220 package=THT]
  D1 = Rectifier Diode [part_number=1N4001 package="300 mil [THT]"]
  D2 = Rectifier Diode [part_number=1N4001 package="300 mil [THT]"]
  R3 = Resistor [tolerance=±5% resistance=68 package=THT]
  R4 = Resistor [tolerance=±5% resistance=1k package=THT]
  X1 = USB Connectors [package=usb-minib]
  AtTiny2313-20PU1 = IC, DIP package, 20 pins [chip_label=AtTiny2313-20PU spacing=300mil]

nets:
  N1: XTAL1.pin_0, AtTiny2313-20PU1.pin4
  N2: XTAL1.pin_1, AtTiny2313-20PU1.pin5
  N3: R1.Pin_0, D1.cathode, X1.D+
  N4: R1.Pin_1, AtTiny2313-20PU1.pin6
  N5: R2.Pin_0, D2.cathode, R3.Pin_0, X1.D-
  N6: R2.Pin_1, R4.Pin_1, X1.VBUS, AtTiny2313-20PU1.pin20
  N7: D1.anode, D2.anode, X1.GND, AtTiny2313-20PU1.pin10
  N8: R3.Pin_1, AtTiny2313-20PU1.pin7
  N9: R4.Pin_0, AtTiny2313-20PU1.pin1
